# Fritzing sketch keyboard (saved by Fritzing 0.9.1b)
breadboards: 1

parts:
  S1 = Pushbutton [package="[THT]"]
  S2 = Pushbutton [package="[THT]"]
  S3 = Pushbutton [package="[THT]"]
  R1 = Resistor [tolerance=±5% resistance=220 package=THT]
  R2 = Resistor [tolerance=±5% resistance=220 package=THT]
  R3 = Resistor [tolerance=±5% resistance=220 package=THT]
  R4 = Resistor [tolerance=±5% resistance=220 package=THT]
  R5 = Resistor [tolerance=±5% resistance=220 package=THT]
  S4 = Pushbutton [package="[THT]"]
  S5 = Pushbutton [package="[THT]"]
  S6 = Pushbutton [package="[THT]"]
  S7 = Pushbutton [package="[THT]"]
  S8 = Pushbutton [package="[THT]"]
  S9 = Pushbutton [package="[THT]"]
  S10 = Pushbutton [package="[THT]"]
  S11 = Pushbutton [package="[THT]"]
  S12 = Pushbutton [package="[THT]"]
  S13 = Pushbutton [package="[THT]"]
  S14 = Pushbutton [package="[THT]"]
  S15 = Pushbutton [package="[THT]"]

nets (from the breadboard view):
  N1: S1.Pin_1, S1.Pin_2, S2.Pin_1, S2.Pin_2, S3.Pin_1, S3.Pin_2, R1.Pin_1, S4.Pin_1, S4.Pin_2
  N2: S1.Pin_3, S1.Pin_4, R2.Pin_0
  N3: S2.Pin_3, S2.Pin_4, R3.Pin_0
  N4: S3.Pin_3, S3.Pin_4, R4.Pin_0
  N5: R2.Pin_1, R4.Pin_1
  N6: R5.Pin_0, S4.Pin_3, S4.Pin_4
  N7: S5.Pin_1, S5.Pin_2
  N8: S5.Pin_3, S5.Pin_4
  N9: S6.Pin_1, S6.Pin_2
  N10: S6.Pin_3, S6.Pin_4
  N11: S7.Pin_1, S7.Pin_2
  N12: S7.Pin_3, S7.Pin_4
  N13: S8.Pin_1, S8.Pin_2
  N14: S8.Pin_3, S8.Pin_4
  N15: S9.Pin_1, S9.Pin_2
  N16: S9.Pin_3, S9.Pin_4
  N17: S10.Pin_1, S10.Pin_2
  N18: S10.Pin_3, S10.Pin_4
  N19: S11.Pin_1, S11.Pin_2
  N20: S11.Pin_3, S11.Pin_4
  N21: S12.Pin_1, S12.Pin_2
  N22: S12.Pin_3, S12.Pin_4
  N23: S13.Pin_1, S13.Pin_2
  N24: S13.Pin_3, S13.Pin_4
  N25: S14.Pin_1, S14.Pin_2
  N26: S14.Pin_3, S14.Pin_4
  N27: S15.Pin_1, S15.Pin_2
  N28: S15.Pin_3, S15.Pin_4
